# Fritzing sketch day3Project3 (saved by Fritzing 0.9.3b)
breadboards: 1

parts:
  Part1 = Arduino Uno (Rev3)
  J1 = Piezo Speaker
  U1 = POT [package=pot_alpha_rv16af-20]
  R1 = Resistor [tolerance=±5% resistance=220 package="0805 [SMD]"]

nets:
  N1: Part1.A0, U1.S
  N2: Part1.5V, U1.A
  N3: Part1.GND, J1.pin1, U1.E
  N4: J1.pin2, R1.Pin_1
