# Fritzing sketch day3Project4 (saved by Fritzing 0.9.3b)
breadboards: 1

parts:
  Part1 = Arduino Uno (Rev3)
  R1 = Photocell (LDR) [package=THT]
  R2 = Resistor [tolerance=±5% resistance=220 package="0805 [SMD]"]
  R3 = Resistor [tolerance=±5% resistance=220 package="1206 [SMD]"]
  LED1 = smd LED [color="Red (633nm)" package="1206 [SMD]"]

nets:
  N1: Part1.A0, R1.pin_0, R2.Pin_1
  N2: Part1.D9_PWM, LED1.anode
  N3: Part1.5V, R1.pin_1
  N4: Part1.GND, R2.Pin_0, R3.Pin_1
  N5: R3.Pin_0, LED1.cathode
