# Fritzing sketch day3Project8 (saved by Fritzing 0.9.3b)
breadboards: 1

parts:
  Part1 = Arduino Uno (Rev3)
  J1 = Basic Servo
  U1 = POT [package=pot_mammoth]

nets:
  N1: Part1.A0, U1.A
  N2: Part1.D9_PWM, J1.pulse
  5V: Part1.5V, J1.vcc, U1.E
  GND: Part1.GND, J1.gnd, U1.S
