# Fritzing sketch button (saved by Fritzing 0.9.3b)
breadboards: 1

parts:
  Part2 = Arduino Uno (Rev3)
  R1 = Resistor [tolerance=±5% resistance=220 package=THT]
  LED1 = smd LED [color="Red (633nm)" package="0603 [SMD]"]
  S1 = Momentary Switch [package=ksa_sealed_tac_switch]

nets:
  N1: Part2.D13/SCK, LED1.anode
  N2: Part2.GND, R1.Pin_1, LED1.cathode
  N3: Part2.5V, S1.4
  N4: R1.Pin_0, S1.1
