# Fritzing sketch single led3 (saved by Fritzing 0.9.3b)
breadboards: 1

parts:
  Part2 = Arduino Uno (Rev3)
  R1 = Resistor [tolerance=±5% resistance=220 package=THT]
  LED2 = smd LED [color="Yellow (595nm)" package="0603 [SMD]"]
  LED3 = smd LED [color="Green (555nm)" package="0603 [SMD]"]
  LED4 = smd LED [color="Red (633nm)" package="0603 [SMD]"]
  R2 = Resistor [tolerance=±5% resistance=220 package=THT]
  R3 = Resistor [tolerance=±5% resistance=220 package=THT]

nets:
  N1: Part2.D11_PWM/MOSI, R1.Pin_0
  N2: Part2.D12/MISO, R2.Pin_0
  N3: Part2.D13/SCK, R3.Pin_0
  N4: Part2.GND, LED2.anode, LED3.anode, LED4.anode
  N5: R1.Pin_1, LED3.cathode
  N6: LED2.cathode, R2.Pin_1
  N7: LED4.cathode, R3.Pin_1
