# Fritzing sketch single multi (saved by Fritzing 0.9.3b)
breadboards: 1

parts:
  Part2 = Arduino Uno (Rev3)
  R5 = Photocell (LDR) [package=THT]
  R9 = Resistor [tolerance=±5% resistance=220 package="1206 [SMD]"]
  R10 = Resistor [tolerance=±5% resistance=220 package="1206 [SMD]"]
  LED1 = RGB LED (com. anode, rbg) [package="5 mm [THT]"]
  R11 = Resistor [tolerance=±5% resistance=220 package="1206 [SMD]"]
  R12 = Resistor [tolerance=±5% resistance=220 package="1206 [SMD]"]

nets:
  N1: Part2.A0, R5.pin_1, R9.Pin_0
  N2: Part2.D12/MISO, R11.Pin_1
  N3: Part2.D13/SCK, R12.Pin_0
  N4: Part2.GND, R5.pin_0, LED1.common_anode
  N5: Part2.5V, R9.Pin_1
  N6: R10.Pin_1, LED1.red_cathode
  N7: LED1.blue_cathode, R11.Pin_0
  N8: LED1.green_cathode, R12.Pin_1
