# Fritzing sketch single rgb.c (saved by Fritzing 0.9.3b)
breadboards: 1

parts:
  Part2 = Arduino Uno (Rev3)
  R1 = Resistor [tolerance=±5% resistance=220 package=THT]
  R2 = Resistor [tolerance=±5% resistance=220 package=THT]
  R3 = Resistor [tolerance=±5% resistance=220 package=THT]
  LED5 = RGB LED (com. cathode, rgb) [package="5 mm [THT]"]
  R4 = Resistor [tolerance=±5% resistance=220 package=THT]

nets:
  N1: Part2.D11_PWM/MOSI, R4.Pin_0
  N2: Part2.D12/MISO, R1.Pin_0
  N3: Part2.D13/SCK, R3.Pin_0
  N4: Part2.GND, R2.Pin_0
  N5: R1.Pin_1, LED5.green_anode
  N6: R2.Pin_1, LED5.common_cathode
  N7: R3.Pin_1, LED5.red_anode
  N8: LED5.blue_anode, R4.Pin_1
